# Fritzing sketch binary_clock (saved by Fritzing 0.9.3b)
circuit board: 9.91102cm x 9.78393cm
breadboards: 1

parts:
  Part1 = Arduino Nano (Rev3.0)
  R1 = Resistor [tolerance=±5% resistance=220 package=THT]
  R2 = Resistor [tolerance=±5% resistance=220 package=THT]
  R3 = Resistor [tolerance=±5% resistance=220 package=THT]
  R4 = Resistor [tolerance=±5% resistance=220 package=THT]
  R5 = Resistor [tolerance=±5% resistance=220 package=THT]
  R6 = Resistor [tolerance=±5% resistance=220 package=THT]
  R7 = Resistor [tolerance=±5% resistance=220 package=THT]
  R8 = Resistor [tolerance=±5% resistance=220 package=THT]
  R9 = Resistor [tolerance=±5% resistance=220 package=THT]
  R10 = Resistor [tolerance=±5% resistance=220 package=THT]
  R11 = Resistor [tolerance=±5% resistance=220 package=THT]
  R12 = Resistor [tolerance=±5% resistance=220 package=THT]
  R13 = Resistor [tolerance=±5% resistance=220 package=THT]
  LED1 = LED - 5mm [color="Red (633nm)" package="5 mm [THT]"]
  LED2 = LED - 5mm [color="Red (633nm)" package="5 mm [THT]"]
  LED3 = LED - 5mm [color="Red (633nm)" package="5 mm [THT]"]
  LED4 = LED - 5mm [color="Red (633nm)" package="5 mm [THT]"]
  LED5 = LED - 5mm [color="Red (633nm)" package="5 mm [THT]"]
  LED6 = LED - 5mm [color="Red (633nm)" package="5 mm [THT]"]
  LED7 = LED - 5mm [color="Red (633nm)" package="5 mm [THT]"]
  LED9 = LED - 5mm [color="Red (633nm)" package="5 mm [THT]"]
  LED10 = LED - 5mm [color="Red (633nm)" package="5 mm [THT]"]
  LED11 = LED - 5mm [color="Red (633nm)" package="5 mm [THT]"]
  LED12 = LED - 5mm [color="Red (633nm)" package="5 mm [THT]"]
  LED13 = LED - 5mm [color="Red (633nm)" package="5 mm [THT]"]
  S1 = Pushbutton [package="[THT]"]
  S2 = Pushbutton [package="[THT]"]
  S3 = Pushbutton [package="[THT]"]
  R14 = Resistor [tolerance=±5% resistance=10k package=THT]
  R15 = Resistor [tolerance=±5% resistance=10k package=THT]
  R16 = Resistor [tolerance=±5% resistance=10k package=THT]
  LED8 = LED - 5mm [color="Red (633nm)" package="5 mm [THT]"]

nets (from the pcb view):
  N1: Part1.GND, R14.Pin_0, R15.Pin_0, R16.Pin_0
  N2: Part1.D2, R1.Pin_1
  N3: Part1.D3, R2.Pin_1
  N4: Part1.D4, R3.Pin_1
  N5: Part1.D5, R4.Pin_1
  N6: Part1.D6, R7.Pin_1
  N7: Part1.D7, R6.Pin_1
  N8: Part1.D8, R5.Pin_1
  N9: Part1.D9, R11.Pin_1
  N10: Part1.D10, R10.Pin_1
  N11: Part1.D11/MOSI, R9.Pin_1
  N12: Part1.D12/MISO, R8.Pin_1
  N13: Part1.5V, S1.Pin_3, S1.Pin_4, S2.Pin_3, S2.Pin_4, S3.Pin_3, S3.Pin_4
  N14: Part1.A7, S3.Pin_1, S3.Pin_2, R14.Pin_1
  N15: Part1.A6, S2.Pin_1, S2.Pin_2, R16.Pin_1
  N16: Part1.A5, S1.Pin_1, S1.Pin_2, R15.Pin_1
  N17: Part1.A1, R12.Pin_1
  N18: Part1.A0, R13.Pin_1
  N19: R1.Pin_0, LED1.anode
  N20: R2.Pin_0, LED2.anode
  N21: R3.Pin_0, LED3.anode
  N22: R4.Pin_0, LED4.anode
  N23: R5.Pin_0, LED5.anode
  N24: R6.Pin_0, LED6.anode
  N25: R7.Pin_0, LED7.anode
  N26: R8.Pin_0, LED8.anode
  N27: R9.Pin_0, LED9.anode
  N28: R10.Pin_0, LED10.anode
  N29: R11.Pin_0, LED11.anode
  N30: R12.Pin_0, LED12.anode
  N31: R13.Pin_0, LED13.anode
  N32: LED1.cathode, LED2.cathode, LED3.cathode, LED4.cathode, LED5.cathode, LED6.cathode, LED7.cathode, LED9.cathode, LED10.cathode, LED11.cathode, LED12.cathode, LED13.cathode, LED8.cathode

notes:
  m. shaw, rev 1, 12/17
